// Digital circuit CPU.dig as structural Verilog
module CPU (
);

  wire A_LD, A_OE, addressdecoder_1_nram_cs, addressdecoder_1_nrom_cs, CLK, MEM_RD, MEM_WR, pc_1_p1, RST;
  wire [2:0] Rdst, Rsrc;
  wire [7:0] pulldown_1_out, ramsingleportsel_1_d, rst_buffer_1_p2;
  wire [15:0] eeprom_1_d;

  ADDRESSDECODER addressdecoder_1 (
    .A_BUS({rst_buffer_1_p2, pulldown_1_out}), .nRAM_CS(addressdecoder_1_nram_cs),
    .nROM_CS(addressdecoder_1_nrom_cs));  // open: nFB_CS, nMMIO_CS
  // RST_Buffer rst_buffer_1: pin names not known; wires that end beside it: RST, rst_buffer_1_p2
  PullDown #(.Bits(8)) pulldown_1 (.out(pulldown_1_out));
  // PC pc_1: pin names not known; wires that end beside it: pc_1_p1, {rst_buffer_1_p2, pulldown_1_out}
  MAR mar_1 (
    .D_BUS(ramsingleportsel_1_d), .RST(RST), .CLK(CLK), .A_BUS({rst_buffer_1_p2, pulldown_1_out}));  // open: nMAR_OE, nMARL_LD, nMARH_LD
  RAMSinglePortSel #(.AddrBits(16), .Bits(8)) ramsingleportsel_1 (
    .A({rst_buffer_1_p2, pulldown_1_out}), .CS(~addressdecoder_1_nram_cs), .WE(MEM_WR), .OE(MEM_RD),
    .D(ramsingleportsel_1_d));
  EEPROM #(.AddrBits(15), .Bits(16)) eeprom_1 (
    .A({1'b0, rst_buffer_1_p2[5:0], pulldown_1_out}), .CS(~addressdecoder_1_nrom_cs), .WE(1'b0), .OE(MEM_RD),
    .D(eeprom_1_d));
  Driver driver_1 (.in(pc_1_p1));  // open: en, out
  RFILE rfile_1 (
    .DB_IN(ramsingleportsel_1_d), .B_10_8(Rdst), .B_7_5(Rsrc), .CLK(CLK), .RST(RST),
    .DB_OUT(ramsingleportsel_1_d), .A_LD(A_LD), .A_OE(A_OE));  // open: REG_LD_EN, REG_OE_EN, nXY_INC, XY_DIR, nXY_AOE, AB_OUT
  // ALU alu_1: pin names not known; wires that end beside it: ramsingleportsel_1_d, A_LD, A_OE, CLK, RST, ramsingleportsel_1_d
  // IR ir_1: pin names not known; wires that end beside it: eeprom_1_d, Rdst, Rsrc

  // Notes on the sheet:
  //   contents of eeprom_1 (hex, n*v repeats v):
  //   2f0,300,101,1500,4300,ac03,ac00,4200,a00,8c10,ac03,ac00
endmodule
