// Digital circuit CTRLUNIT.dig as structural Verilog
module CTRLUNIT (
  input  [7:0] OPC,
  input  [2:0] microstep,
  input  Z,
  input  C,
  input  N,
  input  V,
  input  I,
  output [15:0] C0_15,
  output [15:0] C16_31,
  output [15:0] C32_47
);

  ROM #(.AddrBits(16), .Bits(16)) _1ROM (.A({I, V, N, C, Z, microstep, OPC}), .sel(1'b1), .D(C0_15));
  ROM #(.AddrBits(16), .Bits(16)) _2ROM (.A({I, V, N, C, Z, microstep, OPC}), .sel(1'b1), .D(C16_31));
  ROM #(.AddrBits(16), .Bits(16)) _3ROM (.A({I, V, N, C, Z, microstep, OPC}), .sel(1'b1), .D(C32_47));

  // Notes on the sheet:
  //   contents of _1ROM (hex, n*v repeats v):
  //   256*37da,8*71bb,8*f1fb,8*21bb,8*a1fb,8*747f,8*55ff,8*75ff,8*b87f
  //   ,8*99ff,8*b9ff,16*33fb,8*f1fb,8*71bb,32*f1fb,8*71bb,16*f1fb,16*71bb
  //   ,16*31fb,48*33fb,31fb,31fb,6*33fb,248*33fa,31fa,31fa,254*33fa
  //   ,31fa,31fa,254*33fa,31fa,31fa,254*33fa,31fa,31fa,254*33fa,31fa,31fa
  //   ,254*33fa,31fa,31fa,6*33fa,256*37da,8*71bb,8*f1fb,8*21bb,8*a1fb
  //   ,8*747f,8*55ff,8*75ff,8*b87f,8*99ff,8*b9ff,16*33fb,8*f1fb,8*71bb
  //   ,32*f1fb,8*71bb,16*f1fb,16*71bb,16*31fb,48*33fb,31fb,31fb,6*33fb
  //   ,248*33fa,31fa,31fa,254*33fa,31fa,31fa,254*33fa,31fa,31fa,254*33fa
  //   ,31fa,31fa,254*33fa,31fa,31fa,254*33fa,31fa,31fa,6*33fa,256*37da
  //   ,8*71bb,8*f1fb,8*21bb,8*a1fb,8*747f,8*55ff,8*75ff,8*b87f,8*99ff
  //   ,8*b9ff,16*33fb,8*f1fb,8*71bb,32*f1fb,8*71bb,16*f1fb,16*71bb,16*31fb
  //   ,48*33fb,31fb,31fb,6*33fb,248*33fa,31fa,31fa,254*33fa,31fa,31fa
  //   ,254*33fa,31fa,31fa,254*33fa,31fa,31fa,254*33fa,31fa,31fa,254*33fa
  //   ,31fa,31fa,6*33fa,256*37da,8*71bb,8*f1fb,8*21bb,8*a1fb,8*747f
  //   ,8*55ff,8*75ff,8*b87f,8*99ff,8*b9ff,16*33fb,8*f1fb,8*71bb,32*f1fb
  //   ,8*71bb,16*f1fb,16*71bb,16*31fb,48*33fb,31fb,31fb,6*33fb,248*33fa
  //   ,31fa,31fa,254*33fa,31fa,31fa,254*33fa,31fa,31fa,254*33fa,31fa,31fa
  //   ,254*33fa,31fa,31fa,254*33fa,31fa,31fa,6*33fa,256*37da,8*71bb
  //   ,8*f1fb,8*21bb,8*a1fb,8*747f,8*55ff,8*75ff,8*b87f,8*99ff,8*b9ff
  //   ,16*33fb,8*f1fb,8*71bb,32*f1fb,8*71bb,16*f1fb,16*71bb,16*31fb
  //   ,48*33fb,31fb,31fb,6*33fb,248*33fa,31fa,31fa,254*33fa,31fa,31fa
  //   ,254*33fa,31fa,31fa,254*33fa,31fa,31fa,254*33fa,31fa,31fa,254*33fa
  //   ,31fa,31fa,6*33fa,256*37da,8*71bb,8*f1fb,8*21bb,8*a1fb,8*747f
  //   ,8*55ff,8*75ff,8*b87f,8*99ff,8*b9ff,16*33fb,8*f1fb,8*71bb,32*f1fb
  //   ,8*71bb,16*f1fb,16*71bb,16*31fb,48*33fb,31fb,31fb,6*33fb,248*33fa
  //   ,31fa,31fa,254*33fa,31fa,31fa,254*33fa,31fa,31fa,254*33fa,31fa,31fa
  //   ,254*33fa,31fa,31fa,254*33fa,31fa,31fa,6*33fa,256*37da,8*71bb
  //   ,8*f1fb,8*21bb,8*a1fb,8*747f,8*55ff,8*75ff,8*b87f,8*99ff,8*b9ff
  //   ,16*33fb,8*f1fb,8*71bb,32*f1fb,8*71bb,16*f1fb,16*71bb,16*31fb
  //   ,48*33fb,31fb,31fb,6*33fb,248*33fa,31fa,31fa,254*33fa,31fa,31fa
  //   ,254*33fa,31fa,31fa,254*33fa,31fa,31fa,254*33fa,31fa,31fa,254*33fa
  //   ,31fa,31fa,6*33fa,256*37da,8*71bb,8*f1fb,8*21bb,8*a1fb,8*747f
  //   ,8*55ff,8*75ff,8*b87f,8*99ff,8*b9ff,16*33fb,8*f1fb,8*71bb,32*f1fb
  //   ,8*71bb,16*f1fb,16*71bb,16*31fb,48*33fb,31fb,31fb,6*33fb,248*33fa
  //   ,31fa,31fa,254*33fa,31fa,31fa,254*33fa,31fa,31fa,254*33fa,31fa,31fa
  //   ,254*33fa,31fa,31fa,254*33fa,31fa,31fa,6*33fa,256*37da,8*71bb
  //   ,8*f1fb,8*21bb,8*a1fb,8*747f,8*55ff,8*75ff,8*b87f,8*99ff,8*b9ff
  //   ,16*33fb,8*f1fb,8*71bb,32*f1fb,8*71bb,16*f1fb,16*71bb,16*31fb
  //   ,48*33fb,31fb,31fb,6*33fb,248*33fa,31fa,31fa,254*33fa,31fa,31fa
  //   ,254*33fa,31fa,31fa,254*33fa,31fa,31fa,254*33fa,31fa,31fa,254*33fa
  //   ,31fa,31fa,6*33fa,256*37da,8*71bb,8*f1fb,8*21bb,8*a1fb,8*747f
  //   ,8*55ff,8*75ff,8*b87f,8*99ff,8*b9ff,16*33fb,8*f1fb,8*71bb,32*f1fb
  //   ,8*71bb,16*f1fb,16*71bb,16*31fb,48*33fb,31fb,31fb,6*33fb,248*33fa
  //   ,31fa,31fa,254*33fa,31fa,31fa,254*33fa,31fa,31fa,254*33fa,31fa,31fa
  //   ,254*33fa,31fa,31fa,254*33fa,31fa,31fa,6*33fa,256*37da,8*71bb
  //   ,8*f1fb,8*21bb,8*a1fb,8*747f,8*55ff,8*75ff,8*b87f,8*99ff,8*b9ff
  //   ,16*33fb,8*f1fb,8*71bb,32*f1fb,8*71bb,16*f1fb,16*71bb,16*31fb
  //   ,48*33fb,31fb,31fb,6*33fb,248*33fa,31fa,31fa,254*33fa,31fa,31fa
  //   ,254*33fa,31fa,31fa,254*33fa,31fa,31fa,254*33fa,31fa,31fa,254*33fa
  //   ,31fa,31fa,6*33fa,256*37da,8*71bb,8*f1fb,8*21bb,8*a1fb,8*747f
  //   ,8*55ff,8*75ff,8*b87f,8*99ff,8*b9ff,16*33fb,8*f1fb,8*71bb,32*f1fb
  //   ,8*71bb,16*f1fb,16*71bb,16*31fb,48*33fb,31fb,31fb,6*33fb,248*33fa
  //   ,31fa,31fa,254*33fa,31fa,31fa,254*33fa,31fa,31fa,254*33fa,31fa,31fa
  //   ,254*33fa,31fa,31fa,254*33fa,31fa,31fa,6*33fa,256*37da,8*71bb
  //   ,8*f1fb,8*21bb,8*a1fb,8*747f,8*55ff,8*75ff,8*b87f,8*99ff,8*b9ff
  //   ,16*33fb,8*f1fb,8*71bb,32*f1fb,8*71bb,16*f1fb,16*71bb,16*31fb
  //   ,48*33fb,31fb,31fb,6*33fb,248*33fa,31fa,31fa,254*33fa,31fa,31fa
  //   ,254*33fa,31fa,31fa,254*33fa,31fa,31fa,254*33fa,31fa,31fa,254*33fa
  //   ,31fa,31fa,6*33fa,256*37da,8*71bb,8*f1fb,8*21bb,8*a1fb,8*747f
  //   ,8*55ff,8*75ff,8*b87f,8*99ff,8*b9ff,16*33fb,8*f1fb,8*71bb,32*f1fb
  //   ,8*71bb,16*f1fb,16*71bb,16*31fb,48*33fb,31fb,31fb,6*33fb,248*33fa
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  //   contents of _2ROM (hex, n*v repeats v):
  //   304*da85,8*da81,16*da85,8*da81,16*da85,16*cabd,8*cbbd,8*cbad,8*caad
  //   ,16*caed,8*cadd,8*cacd,8*cbbd,8*caad,8*da84,8*da86,1896*da85,8*da81
  //   ,16*da85,8*da81,16*da85,16*cabd,8*cbbd,8*cbad,8*caad,16*caed,8*cadd
  //   ,8*cacd,8*cbbd,8*caad,8*da84,8*da86,1896*da85,8*da81,16*da85,8*da81
  //   ,16*da85,16*cabd,8*cbbd,8*cbad,8*caad,16*caed,8*cadd,8*cacd,8*cbbd
  //   ,8*caad,8*da84,8*da86,1896*da85,8*da81,16*da85,8*da81,16*da85
  //   ,16*cabd,8*cbbd,8*cbad,8*caad,16*caed,8*cadd,8*cacd,8*cbbd,8*caad
  //   ,8*da84,8*da86,1896*da85,8*da81,16*da85,8*da81,16*da85,16*cabd
  //   ,8*cbbd,8*cbad,8*caad,16*caed,8*cadd,8*cacd,8*cbbd,8*caad,8*da84
  //   ,8*da86,1896*da85,8*da81,16*da85,8*da81,16*da85,16*cabd,8*cbbd
  //   ,8*cbad,8*caad,16*caed,8*cadd,8*cacd,8*cbbd,8*caad,8*da84,8*da86
  //   ,1896*da85,8*da81,16*da85,8*da81,16*da85,16*cabd,8*cbbd,8*cbad
  //   ,8*caad,16*caed,8*cadd,8*cacd,8*cbbd,8*caad,8*da84,8*da86,1896*da85
  //   ,8*da81,16*da85,8*da81,16*da85,16*cabd,8*cbbd,8*cbad,8*caad,16*caed
  //   ,8*cadd,8*cacd,8*cbbd,8*caad,8*da84,8*da86,1896*da85,8*da81,16*da85
  //   ,8*da81,16*da85,16*cabd,8*cbbd,8*cbad,8*caad,16*caed,8*cadd,8*cacd
  //   ,8*cbbd,8*caad,8*da84,8*da86,1896*da85,8*da81,16*da85,8*da81,16*da85
  //   ,16*cabd,8*cbbd,8*cbad,8*caad,16*caed,8*cadd,8*cacd,8*cbbd,8*caad
  //   ,8*da84,8*da86,1896*da85,8*da81,16*da85,8*da81,16*da85,16*cabd
  //   ,8*cbbd,8*cbad,8*caad,16*caed,8*cadd,8*cacd,8*cbbd,8*caad,8*da84
  //   ,8*da86,1896*da85,8*da81,16*da85,8*da81,16*da85,16*cabd,8*cbbd
  //   ,8*cbad,8*caad,16*caed,8*cadd,8*cacd,8*cbbd,8*caad,8*da84,8*da86
  //   ,1896*da85,8*da81,16*da85,8*da81,16*da85,16*cabd,8*cbbd,8*cbad
  //   ,8*caad,16*caed,8*cadd,8*cacd,8*cbbd,8*caad,8*da84,8*da86,1896*da85
  //   ,8*da81,16*da85,8*da81,16*da85,16*cabd,8*cbbd,8*cbad,8*caad,16*caed
  //   ,8*cadd,8*cacd,8*cbbd,8*caad,8*da84,8*da86,1896*da85,8*da81,16*da85
  //   ,8*da81,16*da85,16*cabd,8*cbbd,8*cbad,8*caad,16*caed,8*cadd,8*cacd
  //   ,8*cbbd,8*caad,8*da84,8*da86,1896*da85,8*da81,16*da85,8*da81,16*da85
  //   ,16*cabd,8*cbbd,8*cbad,8*caad,16*caed,8*cadd,8*cacd,8*cbbd,8*caad
  //   ,8*da84,8*da86,1896*da85,8*da81,16*da85,8*da81,16*da85,16*cabd
  //   ,8*cbbd,8*cbad,8*caad,16*caed,8*cadd,8*cacd,8*cbbd,8*caad,8*da84
  //   ,8*da86,1896*da85,8*da81,16*da85,8*da81,16*da85,16*cabd,8*cbbd
  //   ,8*cbad,8*caad,16*caed,8*cadd,8*cacd,8*cbbd,8*caad,8*da84,8*da86
  //   ,1896*da85,8*da81,16*da85,8*da81,16*da85,16*cabd,8*cbbd,8*cbad
  //   ,8*caad,16*caed,8*cadd,8*cacd,8*cbbd,8*caad,8*da84,8*da86,1896*da85
  //   ,8*da81,16*da85,8*da81,16*da85,16*cabd,8*cbbd,8*cbad,8*caad,16*caed
  //   ,8*cadd,8*cacd,8*cbbd,8*caad,8*da84,8*da86,1896*da85,8*da81,16*da85
  //   ,8*da81,16*da85,16*cabd,8*cbbd,8*cbad,8*caad,16*caed,8*cadd,8*cacd
  //   ,8*cbbd,8*caad,8*da84,8*da86,1896*da85,8*da81,16*da85,8*da81,16*da85
  //   ,16*cabd,8*cbbd,8*cbad,8*caad,16*caed,8*cadd,8*cacd,8*cbbd,8*caad
  //   ,8*da84,8*da86,1896*da85,8*da81,16*da85,8*da81,16*da85,16*cabd
  //   ,8*cbbd,8*cbad,8*caad,16*caed,8*cadd,8*cacd,8*cbbd,8*caad,8*da84
  //   ,8*da86,1896*da85,8*da81,16*da85,8*da81,16*da85,16*cabd,8*cbbd
  //   ,8*cbad,8*caad,16*caed,8*cadd,8*cacd,8*cbbd,8*caad,8*da84,8*da86
  //   ,1896*da85,8*da81,16*da85,8*da81,16*da85,16*cabd,8*cbbd,8*cbad
  //   ,8*caad,16*caed,8*cadd,8*cacd,8*cbbd,8*caad,8*da84,8*da86,1896*da85
  //   ,8*da81,16*da85,8*da81,16*da85,16*cabd,8*cbbd,8*cbad,8*caad,16*caed
  //   ,8*cadd,8*cacd,8*cbbd,8*caad,8*da84,8*da86,1896*da85,8*da81,16*da85
  //   ,8*da81,16*da85,16*cabd,8*cbbd,8*cbad,8*caad,16*caed,8*cadd,8*cacd
  //   ,8*cbbd,8*caad,8*da84,8*da86,1896*da85,8*da81,16*da85,8*da81,16*da85
  //   ,16*cabd,8*cbbd,8*cbad,8*caad,16*caed,8*cadd,8*cacd,8*cbbd,8*caad
  //   ,8*da84,8*da86,1896*da85,8*da81,16*da85,8*da81,16*da85,16*cabd
  //   ,8*cbbd,8*cbad,8*caad,16*caed,8*cadd,8*cacd,8*cbbd,8*caad,8*da84
  //   ,8*da86,1896*da85,8*da81,16*da85,8*da81,16*da85,16*cabd,8*cbbd
  //   ,8*cbad,8*caad,16*caed,8*cadd,8*cacd,8*cbbd,8*caad,8*da84,8*da86
  //   ,1896*da85,8*da81,16*da85,8*da81,16*da85,16*cabd,8*cbbd,8*cbad
  //   ,8*caad,16*caed,8*cadd,8*cacd,8*cbbd,8*caad,8*da84,8*da86,1896*da85
  //   ,8*da81,16*da85,8*da81,16*da85,16*cabd,8*cbbd,8*cbad,8*caad,16*caed
  //   ,8*cadd,8*cacd,8*cbbd,8*caad,8*da84,8*da86,1592*da85
  //   contents of _3ROM (hex, n*v repeats v):
  //   65536*7a
endmodule
